// Logisim project TP1_B02.circ as structural Verilog: 1 circuit, main circuit main
module main (
  input  A,
  input  B,
  input  A_2,
  input  A_3,
  input  A_4,
  input  B_2,
  input  A_5,
  input  B_3,
  input  A_6,
  input  B_4
);

  wire pull_resistor_2_node, pull_resistor_3_node, transistor_1_out, transistor_2_out, transistor_6_out,
       transistor_7_out, transistor_11_out, transistor_12_out, transistor_14_out;

  Transistor transistor_1 (.in(1'b0), .out(transistor_1_out), .gate(A_2));
  Pull_Resistor #(.pull(1)) pull_resistor_1 (.node(transistor_1_out));
  Transistor transistor_2 (.in(1'b1), .out(transistor_2_out), .gate(A_3));
  // Probe on transistor_2_out
  Transistor transistor_3 (.in(1'b0), .out(transistor_2_out), .gate(A_3));
  Pull_Resistor #(.pull(1)) pull_resistor_2 (.node(pull_resistor_2_node));
  // Probe on pull_resistor_2_node
  Transistor transistor_4 (.in(1'b0), .out(pull_resistor_2_node), .gate(A_6));
  Transistor #(.gate("br")) transistor_5 (.in(1'b0), .out(pull_resistor_2_node), .gate(B_4));
  Transistor transistor_6 (.in(1'b1), .out(transistor_6_out), .gate(A));
  Transistor transistor_7 (.in(transistor_6_out), .out(transistor_7_out), .gate(B));
  Transistor transistor_8 (.in(1'b0), .out(transistor_7_out), .gate(B));
  Transistor transistor_9 (.in(1'b0), .out(transistor_7_out), .gate(A));
  Pull_Resistor #(.pull(1)) pull_resistor_3 (.node(pull_resistor_3_node));
  Transistor transistor_10 (.in(transistor_11_out), .out(pull_resistor_3_node), .gate(A_4));
  Transistor transistor_11 (.in(1'b0), .out(transistor_11_out), .gate(B_2));
  Transistor transistor_12 (.in(1'b1), .out(transistor_12_out), .gate(A_5));
  Transistor transistor_13 (.in(transistor_14_out), .out(transistor_12_out), .gate(B_3));
  Transistor transistor_14 (.in(1'b0), .out(transistor_14_out), .gate(A_5));
  // Probe on transistor_7_out
  // Probe on pull_resistor_3_node
  // Probe on transistor_12_out
  Transistor transistor_15 (.in(1'b1), .out(transistor_12_out), .gate(B_3));

  // Notes on the sheet:
  //   U0
  //   U1
  //   U2(AND)
  //   U3
  //   U4(OR)
  //   U5
endmodule
